# Fritzing sketch bootspack-tiva-murix-hexacopter (saved by Fritzing 0.8.7b)

parts:
  J1 = Tiva-J1 [form="♀ (female)" package=THT]
  J2 = Tiva-J2 [form="♀ (female)" package=THT]
  Air_Boost_Pack_(915MHz) = Air Boost Pack CC110L [package=1x10-2mm-smd]
  PUSH2 = Pushbutton [package="[SMD]"]
  RESET = Pushbutton [package="[THT]"]
  J3 = Tiva-J3 [form="♀ (female)" package=THT]
  LED-RGB = RGB LED (com. anode, rbg) [package="5 mm [THT]"]
  J4 = Tiva-J4 [form="♀ (female)" package=THT]
  PUSH1 = Pushbutton [package="[SMD]"]
  MPU6050_(I2C) = MPU6050 [package=1x10-2mm-smd]
  HEXACOPTER-MOTOR-1 = DC Motor
  HEXACOPTER-MOTOR-4 = DC Motor
  HEXACOPTER-MOTOR-3 = DC Motor
  HEXACOPTER-MOTOR-2 = DC Motor
  BMP085_(I2C) = BMP85 [package=1x10-2mm-smd]
  HMC5883L_(I2C) = HMC5883L [package=1x10-2mm-smd]
  UBLOX-NEO-6M = UBLOX-NEO-6M [package=1x10-2mm-smd]
  JY-MCU-BLUETOOTH = JY-MCU-BLUETOOTH [package=1x10-2mm-smd]
  VBAT-LIPO-S3-MONITOR = VBAT-MONITOR [package=1x10-2mm-smd]
  SPI-AUX-CC1101-433MHz = SPI-AUX [package=1x10-2mm-smd]
  HEXACOPTER-MOTOR-5 = DC Motor
  HEXACOPTER-MOTOR-6 = DC Motor

nets:
  N1: J1.J1-1-3.3V, Air_Boost_Pack_(915MHz).3.3V
  N2: J1.J1-2-PB5-CS(2)-ADC-PWM, Air_Boost_Pack_(915MHz).GDO2
  N3: J1.J1-3-PB0-PWM-RX(1), JY-MCU-BLUETOOTH.TX
  N4: J1.J1-4-PB1-TX(1)-PWM, JY-MCU-BLUETOOTH.RX
  N5: J1.J1-5-PE4-ADC-SCL(2)-RX(5), HMC5883L_(I2C).SCL
  N6: J1.J1-6-PE5-ADC-SDA(2)-TX(5), HMC5883L_(I2C).SDA
  N7: J1.J1-7-PB4-ADC-PWM-SCK(2), Air_Boost_Pack_(915MHz).SCLK
  N8: J1.J1-8-PA5-MOSI(0), SPI-AUX-CC1101-433MHz.MOSI
  N9: J1.J1-9-PA6-SCL(1), BMP085_(I2C).SCL
  N10: J1.J1-10-PA7-SDA(1), BMP085_(I2C).SDA
  N11: J2.J2-20-GND, Air_Boost_Pack_(915MHz).GND
  N12: J2.J2-19-PB2-PWM-SCL(0), Air_Boost_Pack_(915MHz).GDO0
  N13: J2.J2-18-PE0-ADC-RX(7), Air_Boost_Pack_(915MHz).CS
  N14: J2.J2-17-PF0-MISO(1)-PUSH2, PUSH2.Pin_3, PUSH2.Pin_4
  N15: J2.J2-16-RESET, RESET.Pin_3
  N16: J2.J2-15-PB7-PWM-MOSI(2), Air_Boost_Pack_(915MHz).MOSI
  N17: J2.J2-14-PB6-PWM-MISO(2), Air_Boost_Pack_(915MHz).MISO
  N18: J2.J2-13-MISO(0), SPI-AUX-CC1101-433MHz.MISO
  N19: J2.J2-12-CS(0), SPI-AUX-CC1101-433MHz.CS
  N20: J2.J2-11-SCK(0), SPI-AUX-CC1101-433MHz.SCK
  N21: J3.J3-21-5V, MPU6050_(I2C).5V
  N22: J3.J3-22-GND, MPU6050_(I2C).GND
  N23: J3.J3-23-PD0-PWM-ADC-SCL(3)-SCK(3), MPU6050_(I2C).SCL
  N24: J3.J3-24-PD1-PWM-ADC-SDA(3)-CS(3), MPU6050_(I2C).SDA
  N25: J3.J3-25-PD2-PWM-ADC-MISO(3), HEXACOPTER-MOTOR-5.pin_1, HEXACOPTER-MOTOR-5.pin_2
  N26: J3.J3-26-PD3-PWM-ADC-MOSI(3), HEXACOPTER-MOTOR-6.pin_1
  N27: J3.J3-27-PE1-ADC-TX(7), VBAT-LIPO-S3-MONITOR.S3
  N28: J3.J3-28-PE2-ADC, VBAT-LIPO-S3-MONITOR.S2
  N29: J3.J3-29-PE3-ADC, VBAT-LIPO-S3-MONITOR.S1
  N30: J3.J3-30-PWM-LED-RED-MOSI(1), LED-RGB.red_cathode
  N31: LED-RGB.blue_cathode, J4.J4-40-PF2-BLUE_LED-SCK(1)-PWM
  N32: LED-RGB.green_cathode, J4.J4-39-PF3-PWM-GREEN_LED-CS(1)
  N33: J4.J4-38-PB3-PWM-SDA(0), SPI-AUX-CC1101-433MHz.INT
  N34: J4.J4-37-PC4-PWM-RX(1), UBLOX-NEO-6M.TX
  N35: J4.J4-36-PC5-PWM-TX(1), UBLOX-NEO-6M.RX
  N36: J4.J4-35-PC6-PWM-RX(3), HEXACOPTER-MOTOR-4.pin_1, HEXACOPTER-MOTOR-4.pin_2
  N37: J4.J4-34-PC7-PWM-TX(3), HEXACOPTER-MOTOR-3.pin_1, HEXACOPTER-MOTOR-3.pin_2
  N38: J4.J4-33-PD6-PWM-RX(2), HEXACOPTER-MOTOR-2.pin_1, HEXACOPTER-MOTOR-2.pin_2
  N39: J4.J3-32-PD7-PWM-TX(2), HEXACOPTER-MOTOR-1.pin_1, HEXACOPTER-MOTOR-1.pin_2
  N40: J4.J4-31-PF4-PUSH1, PUSH1.Pin_3, PUSH1.Pin_4
