# Fritzing sketch bootspack-tiva-murix-quad (saved by Fritzing 0.8.7b)
circuit board: 16.1381cm x 10.8906cm

parts:
  TIVA-J1 = Tiva-J1 [form="♀ (female)" package=THT]
  TIVA-J2 = Tiva-J2 [form="♀ (female)" package=THT]
  PUSH2_(GPIO) = Pushbutton [package="[SMD]"]
  RESET = Pushbutton [package="[THT]"]
  TIVA-J3 = Tiva-J3 [form="♀ (female)" package=THT]
  TIVA-J4 = Tiva-J4 [form="♀ (female)" package=THT]
  PUSH1_(GPIO) = Pushbutton [package="[SMD]"]
  MPU6050_(I2C) = MPU6050 [package=1x10-2mm-smd]
  QUAD-ESC-4_(PWM) = DC Motor
  QUAD-ESC-1_(PWM) = DC Motor
  QUAD-ESC-2_(PWM) = DC Motor
  QUAD-ESC-3_(PWM) = DC Motor
  BMP085_(I2C) = BMP85 [package=1x10-2mm-smd]
  GY-273_/_HMC5883L_(I2C) = HMC5883L [package=1x10-2mm-smd]
  BATTERY-VOLTMETER_(_3_ADC) = VBAT-MONITOR [package=1x10-2mm-smd]
  HC-SR04_/_SONAR_-_(2_GPIO) = HC-SR04 [package=1x10-2mm-smd]
  GY-GPS6MV1/UBLOX_NEO_6M_(USART) = UBLOX-NEO-6M [package=1x10-2mm-smd]
  LED-RGB_(_3_PWM) = RGB LED (com. anode, rbg) [package="5 mm [THT]"]
  HC-06_/_BLUETOOTH_(USART) = JY-MCU-BLUETOOTH [package=1x10-2mm-smd]
  Air_Boost_Pack_-_J1_(SPI+GPIO) = Air Boost Pack CC110L - J1 [package=1x10-2mm-smd]
  Air_Boost_Pack_-_J2_(SPI+GPIO) = Air Boost Pack CC110L - J2 [package=1x10-2mm-smd]

nets (from the breadboard view):
  N1: TIVA-J1.J1-1-3.3V, Air_Boost_Pack_-_J1_(SPI+GPIO).3.3V
  N2: TIVA-J1.J1-2-PB5-CS(2)-ADC-PWM, Air_Boost_Pack_-_J1_(SPI+GPIO).GDO2
  N3: TIVA-J1.J1-3-PB0-PWM-RX(1), GY-GPS6MV1/UBLOX_NEO_6M_(USART).TX
  N4: TIVA-J1.J1-4-PB1-TX(1)-PWM, GY-GPS6MV1/UBLOX_NEO_6M_(USART).RX
  N5: TIVA-J1.J1-5-PE4-ADC-SCL(2)-RX(5), GY-273_/_HMC5883L_(I2C).SCL
  N6: TIVA-J1.J1-6-PE5-ADC-SDA(2)-TX(5), GY-273_/_HMC5883L_(I2C).SDA
  N7: TIVA-J1.J1-7-PB4-ADC-PWM-SCK(2), Air_Boost_Pack_-_J1_(SPI+GPIO).SCK
  N8: TIVA-J1.J1-9-PA6-SCL(1), BMP085_(I2C).SCL
  N9: TIVA-J1.J1-10-PA7-SDA(1), BMP085_(I2C).SDA
  N10: TIVA-J2.J2-20-GND, Air_Boost_Pack_-_J2_(SPI+GPIO).GND
  N11: TIVA-J2.J2-19-PB2-PWM-SCL(0), Air_Boost_Pack_-_J2_(SPI+GPIO).GDO0
  N12: TIVA-J2.J2-18-PE0-ADC-RX(7), Air_Boost_Pack_-_J2_(SPI+GPIO).CSN
  N13: TIVA-J2.J2-17-PF0-MISO(1)-PUSH2, PUSH2_(GPIO).Pin_3, PUSH2_(GPIO).Pin_4
  N14: TIVA-J2.J2-16-RESET, RESET.Pin_3, RESET.Pin_4
  N15: TIVA-J2.J2-15-PB7-PWM-MOSI(2), Air_Boost_Pack_-_J2_(SPI+GPIO).SI
  N16: TIVA-J2.J2-14-PB6-PWM-MISO(2), Air_Boost_Pack_-_J2_(SPI+GPIO).SO
  N17: TIVA-J3.J3-21-5V, MPU6050_(I2C).5V
  N18: TIVA-J3.J3-22-GND, MPU6050_(I2C).GND
  N19: TIVA-J3.J3-23-PD0-PWM-ADC-SCL(3)-SCK(3), MPU6050_(I2C).SCL
  N20: TIVA-J3.J3-24-PD1-PWM-ADC-SDA(3)-CS(3), MPU6050_(I2C).SDA
  N21: TIVA-J3.J3-25-PD2-PWM-ADC-MISO(3), HC-SR04_/_SONAR_-_(2_GPIO).TRIGGER
  N22: TIVA-J3.J3-26-PD3-PWM-ADC-MOSI(3), HC-SR04_/_SONAR_-_(2_GPIO).ECHO
  N23: TIVA-J3.J3-27-PE1-ADC-TX(7), BATTERY-VOLTMETER_(_3_ADC).S3
  N24: TIVA-J3.J3-28-PE2-ADC, BATTERY-VOLTMETER_(_3_ADC).S2
  N25: TIVA-J3.J3-29-PE3-ADC, BATTERY-VOLTMETER_(_3_ADC).S1
  N26: TIVA-J3.J3-30-PWM-LED-RED-MOSI(1), LED-RGB_(_3_PWM).red_cathode
  N27: TIVA-J4.J4-40-PF2-BLUE_LED-SCK(1)-PWM, LED-RGB_(_3_PWM).green_cathode
  N28: TIVA-J4.J4-39-PF3-PWM-GREEN_LED-CS(1), LED-RGB_(_3_PWM).blue_cathode
  N29: TIVA-J4.J4-37-PC4-PWM-RX(1), HC-06_/_BLUETOOTH_(USART).TX
  N30: TIVA-J4.J4-36-PC5-PWM-TX(1), HC-06_/_BLUETOOTH_(USART).RX
  N31: TIVA-J4.J4-35-PC6-PWM-RX(3), QUAD-ESC-1_(PWM).pin_1, QUAD-ESC-1_(PWM).pin_2
  N32: TIVA-J4.J4-34-PC7-PWM-TX(3), QUAD-ESC-2_(PWM).pin_1, QUAD-ESC-2_(PWM).pin_2
  N33: TIVA-J4.J4-33-PD6-PWM-RX(2), QUAD-ESC-3_(PWM).pin_1, QUAD-ESC-3_(PWM).pin_2
  N34: TIVA-J4.J3-32-PD7-PWM-TX(2), QUAD-ESC-4_(PWM).pin_1, QUAD-ESC-4_(PWM).pin_2
  N35: TIVA-J4.J4-31-PF4-PUSH1, PUSH1_(GPIO).Pin_1, PUSH1_(GPIO).Pin_2
  N36: PUSH1_(GPIO).Pin_3, PUSH1_(GPIO).Pin_4
